// Logisim project processador_monociclo.circ as structural Verilog: 4 circuits, main circuit PROCESSADOR
module BANCO_DE_REGISTRADORES (
  input  [31:0] DATA_WRITE,
  input  [3:0] R0,
  input  CLK,
  input  RESET,
  input  [3:0] R1,
  input  RW,
  input  [3:0] RW_2,
  output [31:0] R0_D,
  output [31:0] R1_D
);

  wire demultiplexer_1_out0, demultiplexer_1_out1, demultiplexer_1_out2, demultiplexer_1_out3,
       demultiplexer_1_out4, demultiplexer_1_out5, demultiplexer_1_out6, demultiplexer_1_out7,
       demultiplexer_1_out8, demultiplexer_1_out9, demultiplexer_1_out10, demultiplexer_1_out11,
       demultiplexer_1_out12, demultiplexer_1_out13, demultiplexer_1_out14, demultiplexer_1_out15;
  wire [31:0] _0000, _0001, _0010, _0011, _0100, _0101, _0110, _0111, _1000, _1001, _1010, _1011, _1100,
       _1101, _1110, _1111;

  Demultiplexer #(.select(4), .enable("false")) demultiplexer_1 (
    .out0(demultiplexer_1_out0), .out1(demultiplexer_1_out1), .out2(demultiplexer_1_out2),
    .out3(demultiplexer_1_out3), .out4(demultiplexer_1_out4), .out5(demultiplexer_1_out5),
    .out6(demultiplexer_1_out6), .out7(demultiplexer_1_out7), .out8(demultiplexer_1_out8),
    .out9(demultiplexer_1_out9), .out10(demultiplexer_1_out10), .out11(demultiplexer_1_out11),
    .out12(demultiplexer_1_out12), .out13(demultiplexer_1_out13), .out14(demultiplexer_1_out14),
    .out15(demultiplexer_1_out15), .in(RW), .sel(RW_2));
  Register #(.width(32)) register_1 (.D(DATA_WRITE), .Q(_0000), .clr(demultiplexer_1_out0));  // open: en, clk
  Register #(.width(32)) register_2 (.D(DATA_WRITE), .en(demultiplexer_1_out1), .Q(_0001), .clk(CLK), .clr(RESET));
  Register #(.width(32)) register_3 (.D(DATA_WRITE), .en(demultiplexer_1_out2), .Q(_0010), .clk(CLK), .clr(RESET));
  Register #(.width(32)) register_4 (.D(DATA_WRITE), .en(demultiplexer_1_out3), .Q(_0011), .clk(CLK), .clr(RESET));
  Register #(.width(32)) register_5 (.D(DATA_WRITE), .en(demultiplexer_1_out4), .Q(_0100), .clk(CLK), .clr(RESET));
  Register #(.width(32)) register_6 (.D(DATA_WRITE), .en(demultiplexer_1_out5), .Q(_0101), .clk(CLK), .clr(RESET));
  Register #(.width(32)) register_7 (.D(DATA_WRITE), .en(demultiplexer_1_out6), .Q(_0110), .clk(CLK), .clr(RESET));
  Register #(.width(32)) register_8 (.D(DATA_WRITE), .en(demultiplexer_1_out7), .Q(_0111), .clk(CLK), .clr(RESET));
  Register #(.width(32)) register_9 (.D(DATA_WRITE), .en(demultiplexer_1_out8), .Q(_1000), .clk(CLK), .clr(RESET));
  Register #(.width(32)) register_10 (.D(DATA_WRITE), .en(demultiplexer_1_out9), .Q(_1001), .clk(CLK), .clr(RESET));
  Register #(.width(32)) register_11 (.D(DATA_WRITE), .en(demultiplexer_1_out10), .Q(_1010), .clk(CLK), .clr(RESET));
  Register #(.width(32)) register_12 (.D(DATA_WRITE), .en(demultiplexer_1_out11), .Q(_1011), .clk(CLK), .clr(RESET));
  Register #(.width(32)) register_13 (.D(DATA_WRITE), .en(demultiplexer_1_out12), .Q(_1100), .clk(CLK), .clr(RESET));
  Register #(.width(32)) register_14 (.D(DATA_WRITE), .en(demultiplexer_1_out13), .Q(_1101), .clk(CLK), .clr(RESET));
  Register #(.width(32)) register_15 (.D(DATA_WRITE), .en(demultiplexer_1_out14), .Q(_1110), .clk(CLK), .clr(RESET));
  Register #(.width(32)) register_16 (.D(DATA_WRITE), .en(demultiplexer_1_out15), .Q(_1111), .clk(CLK), .clr(RESET));
  Multiplexer #(.select(4), .width(32), .disabled(0), .enable("false")) multiplexer_1 (
    .in0(_0000), .in1(_0001), .in2(_0010), .in3(_0011), .in4(_0100), .in5(_0101), .in6(_0110), .in7(_0111),
    .in8(_1000), .in9(_1001), .in10(_1010), .in11(_1011), .in12(_1100), .in13(_1101), .in14(_1110),
    .in15(_1111), .out(R0_D), .sel(R0));
  Multiplexer #(.select(4), .width(32), .disabled(0), .enable("false")) multiplexer_2 (
    .in0(_0000), .in1(_0001), .in2(_0010), .in3(_0011), .in4(_0100), .in5(_0101), .in6(_0110), .in7(_0111),
    .in8(_1000), .in9(_1001), .in10(_1010), .in11(_1011), .in12(_1100), .in13(_1101), .in14(_1110),
    .in15(_1111), .out(R1_D), .sel(R1));

  // Other names for the same wires on the sheet: R = RESET; White[31:0] = DATA_WRITE
endmodule

module PROCESSADOR (
  output [31:0] \INSTRUÇÃO 
);

  wire and_1_out, button_1_out, clock_1_out, MUX_ULA, or_1_out, UC_branch, UC_jump, UC_mem_read,
       UC_mem_write, UC_write_reg, ula_1_bge;
  wire [3:0] UC_op_code;
  wire [31:0] adder_1_out, banco_de_registradores_1_r0_d, banco_de_registradores_1_r1_d, bit_extender_1_out,
       bit_extender_2_out, multiplexer_1_out, multiplexer_2_out, multiplexer_3_out, PC_q, ram_1_data,
       ula_1_ula_out;

  Adder #(.width(32)) adder_1 (.a(PC_q), .b(32'h4), .out(adder_1_out));  // open: cin, cout
  assign bit_extender_1_out = {{16{1'b0}}, \INSTRUÇÃO [15:0]};  // Bit_Extender bit_extender_1
  Multiplexer #(.width(32), .enable("false")) multiplexer_1 (
    .in0(adder_1_out), .in1(bit_extender_1_out), .out(multiplexer_1_out), .sel(or_1_out));
  or or_1 (or_1_out, UC_jump, and_1_out);
  and and_1 (and_1_out, UC_branch, ula_1_bge);
  Clock clock_1 (.out(clock_1_out));
  Register #(.width(32)) PC (.D(multiplexer_1_out), .Q(PC_q), .clk(clock_1_out), .clr(button_1_out));  // open: en
  Button button_1 (.out(button_1_out));
  ROM #(.dataWidth(32)) rom_1 (.addr(PC_q[9:2]), .data(\INSTRUÇÃO ));  // open: sel
  UC UC (
    .E3(\INSTRUÇÃO [31]), .E2(\INSTRUÇÃO [30]), .E1(\INSTRUÇÃO [29]), .E0(\INSTRUÇÃO [28]),
    .write_reg(UC_write_reg), .mux_ula(MUX_ULA), .branch(UC_branch), .jump(UC_jump), .mem_read(UC_mem_read),
    .mem_write(UC_mem_write), .op_code(UC_op_code));
  BANCO_DE_REGISTRADORES banco_de_registradores_1 (
    .DATA_WRITE(multiplexer_3_out), .CLK(clock_1_out), .R0_D(banco_de_registradores_1_r0_d),
    .R0(\INSTRUÇÃO [19:16]), .R1_D(banco_de_registradores_1_r1_d), .R1(\INSTRUÇÃO [23:20]),
    .RW(UC_write_reg), .RESET(button_1_out), .RW_2(\INSTRUÇÃO [27:24]));
  assign bit_extender_2_out = {{16{1'b0}}, \INSTRUÇÃO [15:0]};  // Bit_Extender bit_extender_2
  Multiplexer #(.width(32), .enable("false")) multiplexer_2 (
    .in0(banco_de_registradores_1_r1_d), .in1(bit_extender_2_out), .out(multiplexer_2_out), .sel(MUX_ULA));
  ULA ula_1 (
    .DATA_0(banco_de_registradores_1_r0_d), .DATA_1(multiplexer_2_out), .ULA_OUT(ula_1_ula_out),
    .ULA_OP(UC_op_code), .shamt(\INSTRUÇÃO [15:11]), .bge(ula_1_bge));
  Multiplexer #(.width(32), .enable("false")) multiplexer_3 (
    .in0(ula_1_ula_out), .in1(ram_1_data), .out(multiplexer_3_out), .sel(UC_mem_read));
  RAM #(.addrWidth(24), .dataWidth(32), .bus("separate")) ram_1 (
    .addr(banco_de_registradores_1_r0_d[23:0]), .din(banco_de_registradores_1_r1_d), .data(ram_1_data),
    .str(UC_mem_write), .clk(clock_1_out), .ld(UC_mem_read), .clr(button_1_out));  // open: sel

  // Other names for the same wires on the sheet: SHAMT[4:0] = \INSTRUÇÃO [15:11]

  // Notes on the sheet:
  //   contents of rom_1 (hex, n*v repeats v):
  //   6a000000 61000000 62000000 6f000002 6b000000 6c000004 6d000008 50af008c 61000000 501f0084 62000000
  //   63000000 29af0000 9910000 ed90000 700e0000 502f0074 28af0000 8820000 eb80000 840e0000 272f0000
  //   7710000 ec70000 850e0000 26450000 3360000 32020001 40000040 ed90000 703e0000 31010001 40000024
  //   3a0a0001 4000001c
  //   SHAMT
  //   REG_W
  //   REG_1
  //   REG_0
  //   DATA_W
  //   BANCO DE REGISTRADORES
  //   REG1_D
  //   REG0_D
  //   ULA
endmodule

module ULA (
  input  [31:0] DATA_0,
  input  [31:0] DATA_1,
  input  [3:0] ULA_OP,
  input  [4:0] shamt,
  output [31:0] ULA_OUT,
  output bge
);

  wire comparator_1_lt;
  wire [31:0] adder_1_out, multiplier_1_out, shifter_1_out, shifter_2_out, subtractor_1_out;

  Adder #(.width(32)) adder_1 (.a(DATA_0), .b(DATA_1), .out(adder_1_out));  // open: cin, cout
  Subtractor #(.width(32)) subtractor_1 (.a(DATA_1), .b(DATA_0), .out(subtractor_1_out));  // open: bin, bout
  Multiplier #(.width(32)) multiplier_1 (.a(DATA_1), .b(DATA_0), .out(multiplier_1_out));  // open: cin, cout
  Comparator #(.width(32), .mode("unsigned")) comparator_1 (
    .a(DATA_1), .b(DATA_0), .lt(comparator_1_lt));  // open: gt, eq
  Shifter #(.width(32)) shifter_1 (.in(DATA_0), .\dist (shamt), .out(shifter_1_out));
  Shifter #(.width(32), .shift("lr")) shifter_2 (.in(DATA_0), .\dist (shamt), .out(shifter_2_out));
  not not_1 (bge, comparator_1_lt);
  Multiplexer #(.select(4), .width(32)) multiplexer_1 (
    .in0(adder_1_out), .in1(subtractor_1_out), .in2(multiplier_1_out), .in3(adder_1_out),
    .in4(shifter_1_out), .in6(adder_1_out), .in8(shifter_2_out), .out(ULA_OUT), .sel(ULA_OP));  // open: in5, in7, in9, in10, in11, in12, in13, in14, in15, en
endmodule

module UC (
  input  E3,
  input  E2,
  input  E1,
  input  E0,
  output write_reg,
  output mux_ula,
  output branch,
  output jump,
  output mem_read,
  output mem_write,
  output [3:0] op_code
);

  wire and_1_out, and_2_out, and_3_out, not_1_out, not_2_out, not_3_out, not_4_out, not_5_out, not_6_out,
       not_7_out;

  not not_1 (not_1_out, E2);
  and and_1 (and_1_out, E1, not_2_out);
  not not_2 (not_2_out, E0);
  not not_3 (not_3_out, E2);
  and and_2 (and_2_out, not_3_out, E1, E0);
  and and_3 (and_3_out, E2, E1, not_4_out);
  not not_4 (not_4_out, E0);
  and and_4 (branch, E2, not_5_out, E0);
  not not_5 (not_5_out, E1);
  not not_6 (not_6_out, E1);
  and and_5 (jump, E2, not_6_out, not_7_out);
  not not_7 (not_7_out, E0);
  and and_6 (mem_write, E2, E1, E0);
  or or_1 (write_reg, not_1_out, and_1_out);
  or or_2 (mux_ula, and_2_out, and_3_out);

  assign mem_read = E3;
  assign op_code = {E3, E2, E1, E0};
endmodule
