// Logisim project Processador_pipeline.circ as structural Verilog: 5 circuits, main circuit PROCESSADOR
module BANCO_DE_REGISTRADORES (
  input  [31:0] DATA_WRITE,
  input  [3:0] R0,
  input  CLK,
  input  RESET,
  input  [3:0] R1,
  input  RW,
  input  [3:0] RW_2,
  output [31:0] R0_D,
  output [31:0] R1_D
);

  wire demultiplexer_1_out0, demultiplexer_1_out1, demultiplexer_1_out2, demultiplexer_1_out3,
       demultiplexer_1_out4, demultiplexer_1_out5, demultiplexer_1_out6, demultiplexer_1_out7,
       demultiplexer_1_out8, demultiplexer_1_out9, demultiplexer_1_out10, demultiplexer_1_out11,
       demultiplexer_1_out12, demultiplexer_1_out13, demultiplexer_1_out14, demultiplexer_1_out15;
  wire [31:0] _0000, _0001, _0010, _0011, _0100, _0101, _0110, _0111, _1000, _1001, _1010, _1011, _1100,
       _1101, _1110, _1111;

  Demultiplexer #(.select(4), .enable("false")) demultiplexer_1 (
    .out0(demultiplexer_1_out0), .out1(demultiplexer_1_out1), .out2(demultiplexer_1_out2),
    .out3(demultiplexer_1_out3), .out4(demultiplexer_1_out4), .out5(demultiplexer_1_out5),
    .out6(demultiplexer_1_out6), .out7(demultiplexer_1_out7), .out8(demultiplexer_1_out8),
    .out9(demultiplexer_1_out9), .out10(demultiplexer_1_out10), .out11(demultiplexer_1_out11),
    .out12(demultiplexer_1_out12), .out13(demultiplexer_1_out13), .out14(demultiplexer_1_out14),
    .out15(demultiplexer_1_out15), .in(RW), .sel(RW_2));
  Register #(.width(32)) register_1 (.D(DATA_WRITE), .Q(_0000), .clr(demultiplexer_1_out0));  // open: en, clk
  Register #(.width(32)) register_2 (.D(DATA_WRITE), .en(demultiplexer_1_out1), .Q(_0001), .clk(CLK), .clr(RESET));
  Register #(.width(32)) register_3 (.D(DATA_WRITE), .en(demultiplexer_1_out2), .Q(_0010), .clk(CLK), .clr(RESET));
  Register #(.width(32)) register_4 (.D(DATA_WRITE), .en(demultiplexer_1_out3), .Q(_0011), .clk(CLK), .clr(RESET));
  Register #(.width(32)) register_5 (.D(DATA_WRITE), .en(demultiplexer_1_out4), .Q(_0100), .clk(CLK), .clr(RESET));
  Register #(.width(32)) register_6 (.D(DATA_WRITE), .en(demultiplexer_1_out5), .Q(_0101), .clk(CLK), .clr(RESET));
  Register #(.width(32)) register_7 (.D(DATA_WRITE), .en(demultiplexer_1_out6), .Q(_0110), .clk(CLK), .clr(RESET));
  Register #(.width(32)) register_8 (.D(DATA_WRITE), .en(demultiplexer_1_out7), .Q(_0111), .clk(CLK), .clr(RESET));
  Register #(.width(32)) register_9 (.D(DATA_WRITE), .en(demultiplexer_1_out8), .Q(_1000), .clk(CLK), .clr(RESET));
  Register #(.width(32)) register_10 (.D(DATA_WRITE), .en(demultiplexer_1_out9), .Q(_1001), .clk(CLK), .clr(RESET));
  Register #(.width(32)) register_11 (.D(DATA_WRITE), .en(demultiplexer_1_out10), .Q(_1010), .clk(CLK), .clr(RESET));
  Register #(.width(32)) register_12 (.D(DATA_WRITE), .en(demultiplexer_1_out11), .Q(_1011), .clk(CLK), .clr(RESET));
  Register #(.width(32)) register_13 (.D(DATA_WRITE), .en(demultiplexer_1_out12), .Q(_1100), .clk(CLK), .clr(RESET));
  Register #(.width(32)) register_14 (.D(DATA_WRITE), .en(demultiplexer_1_out13), .Q(_1101), .clk(CLK), .clr(RESET));
  Register #(.width(32)) register_15 (.D(DATA_WRITE), .en(demultiplexer_1_out14), .Q(_1110), .clk(CLK), .clr(RESET));
  Register #(.width(32)) register_16 (.D(DATA_WRITE), .en(demultiplexer_1_out15), .Q(_1111), .clk(CLK), .clr(RESET));
  Multiplexer #(.select(4), .width(32), .disabled(0), .enable("false")) multiplexer_1 (
    .in0(_0000), .in1(_0001), .in2(_0010), .in3(_0011), .in4(_0100), .in5(_0101), .in6(_0110), .in7(_0111),
    .in8(_1000), .in9(_1001), .in10(_1010), .in11(_1011), .in12(_1100), .in13(_1101), .in14(_1110),
    .in15(_1111), .out(R0_D), .sel(R0));
  Multiplexer #(.select(4), .width(32), .disabled(0), .enable("false")) multiplexer_2 (
    .in0(_0000), .in1(_0001), .in2(_0010), .in3(_0011), .in4(_0100), .in5(_0101), .in6(_0110), .in7(_0111),
    .in8(_1000), .in9(_1001), .in10(_1010), .in11(_1011), .in12(_1100), .in13(_1101), .in14(_1110),
    .in15(_1111), .out(R1_D), .sel(R1));

  // Other names for the same wires on the sheet: R = RESET; White[31:0] = DATA_WRITE
endmodule

module PROCESSADOR (
  output [31:0] \INSTRUÇÃO 
);

  wire and_1_out, CLK, j, MUX_ULA, or_1_out, R, register_13_q, register_14_q, register_18_q, ula_1_bge,
       write_reg;
  wire [3:0] multiplexer_3_out, register_3_q, register_4_q, register_5_q, register_7_q, UC_op_code;
  wire [4:0] SHAMT;
  wire [5:0] register_6_q, UC_write_reg;
  wire [15:0] multiplexer_1_out, register_1_q;
  wire [31:0] adder_1_out, banco_de_registradores_1_r0_d, banco_de_registradores_1_r1_d, bit_extender_1_out,
       bit_extender_2_out, multiplexer_2_out, multiplexer_4_out, multiplexer_5_out, PC_q, ram_1_data,
       register_8_q, register_10_q, register_11_q, register_15_q, register_16_q, register_17_q,
       register_19_q, rom_1_data, ula_1_ula_out;

  Register #(.width(16)) register_1 (.D(\INSTRUÇÃO [15:0]), .Q(register_1_q), .clk(CLK), .clr(R));  // open: en
  Adder #(.width(32)) adder_1 (.a(PC_q), .b(32'h4), .out(adder_1_out));  // open: cin, cout
  Multiplexer #(.width(16), .enable("false")) multiplexer_1 (
    .in0(register_1_q), .in1(rom_1_data[15:0]), .out(multiplexer_1_out), .sel(j));
  assign bit_extender_1_out = {{16{1'b0}}, multiplexer_1_out};  // Bit_Extender bit_extender_1
  Multiplexer #(.width(32), .enable("false")) multiplexer_2 (
    .in0(adder_1_out), .in1(bit_extender_1_out), .out(multiplexer_2_out), .sel(or_1_out));
  or or_1 (or_1_out, j, and_1_out);
  and and_1 (and_1_out, register_6_q[2], ula_1_bge);
  Register #(.width(32)) PC (.D(multiplexer_2_out), .Q(PC_q), .clk(CLK), .clr(R));  // open: en
  UC_LITTLE uc_little_1 (.e3(rom_1_data[31]), .e2(rom_1_data[30]), .e1(rom_1_data[29]), .e0(rom_1_data[28]), .j(j));
  ROM #(.dataWidth(32)) rom_1 (.addr(PC_q[9:2]), .data(rom_1_data));  // open: sel
  Register #(.width(32)) register_2 (.D(rom_1_data), .Q(\INSTRUÇÃO ), .clk(CLK), .clr(R));  // open: en
  UC UC (
    .E3(\INSTRUÇÃO [31]), .E2(\INSTRUÇÃO [30]), .E1(\INSTRUÇÃO [29]), .E0(\INSTRUÇÃO [28]),
    .write_reg(UC_write_reg[0]), .mux_ula(UC_write_reg[1]), .branch(UC_write_reg[2]), .jump(UC_write_reg[3]),
    .mem_read(UC_write_reg[4]), .mem_write(UC_write_reg[5]), .op_code(UC_op_code));
  assign bit_extender_2_out = {{16{1'b0}}, \INSTRUÇÃO [15:0]};  // Bit_Extender bit_extender_2
  Register #(.width(4)) register_3 (.D(\INSTRUÇÃO [27:24]), .Q(register_3_q), .clk(CLK), .clr(R));  // open: en
  Register #(.width(4)) register_4 (.D(register_3_q), .Q(register_4_q), .clk(CLK), .clr(R));  // open: en
  Register #(.width(4)) register_5 (.D(register_4_q), .Q(register_5_q), .clk(CLK), .clr(R));  // open: en
  Multiplexer #(.width(4), .enable("false")) multiplexer_3 (
    .in0(register_4_q), .in1(register_5_q), .out(multiplexer_3_out), .sel(register_18_q));
  BANCO_DE_REGISTRADORES banco_de_registradores_1 (
    .DATA_WRITE(multiplexer_5_out), .CLK(CLK), .R0_D(banco_de_registradores_1_r0_d), .R0(\INSTRUÇÃO [19:16]),
    .R1_D(banco_de_registradores_1_r1_d), .R1(\INSTRUÇÃO [23:20]), .RW(write_reg), .RESET(R),
    .RW_2(multiplexer_3_out));
  Clock clock_1 (.out(CLK));
  Button button_1 (.out(R));
  Register #(.width(6)) register_6 (
    .D(UC_write_reg), .Q({register_6_q[5:2], MUX_ULA, register_6_q[0]}), .clk(CLK), .clr(R));  // open: en
  Register #(.width(4)) register_7 (.D(UC_op_code), .Q(register_7_q), .clk(CLK), .clr(R));  // open: en
  Register #(.width(32)) register_8 (.D(bit_extender_2_out), .Q(register_8_q), .clk(CLK), .clr(R));  // open: en
  Register #(.width(5)) register_9 (.D(\INSTRUÇÃO [15:11]), .Q(SHAMT), .clk(CLK), .clr(R));  // open: en
  Register #(.width(32)) register_10 (
    .D(banco_de_registradores_1_r1_d), .Q(register_10_q), .clk(CLK), .clr(R));  // open: en
  Register #(.width(32)) register_11 (
    .D(banco_de_registradores_1_r0_d), .Q(register_11_q), .clk(CLK), .clr(R));  // open: en
  Multiplexer #(.width(32), .enable("false")) multiplexer_4 (
    .in0(register_10_q), .in1(register_8_q), .out(multiplexer_4_out), .sel(MUX_ULA));
  ULA ula_1 (
    .DATA_0(register_11_q), .DATA_1(multiplexer_4_out), .ULA_OUT(ula_1_ula_out), .ULA_OP(register_7_q),
    .shamt(SHAMT), .bge(ula_1_bge));
  Multiplexer #(.width(32), .enable("false")) multiplexer_5 (
    .in0(register_16_q), .in1(register_19_q), .out(multiplexer_5_out), .sel(register_18_q));
  Register #(.width(1)) register_12 (.D(register_6_q[0]), .Q(write_reg), .clk(CLK), .clr(R));  // open: en
  Register #(.width(1)) register_13 (.D(register_6_q[4]), .Q(register_13_q), .clk(CLK), .clr(R));  // open: en
  Register #(.width(1)) register_14 (.D(register_6_q[5]), .Q(register_14_q), .clk(CLK), .clr(R));  // open: en
  Register #(.width(32)) register_15 (.D(register_10_q), .Q(register_15_q), .clk(CLK), .clr(R));  // open: en
  Register #(.width(32)) register_16 (.D(ula_1_ula_out), .Q(register_16_q), .clk(CLK), .clr(R));  // open: en
  Register #(.width(32)) register_17 (.D(register_11_q), .Q(register_17_q), .clk(CLK), .clr(R));  // open: en
  RAM #(.addrWidth(24), .dataWidth(32), .bus("separate")) ram_1 (
    .addr(register_17_q[23:0]), .din(register_15_q), .data(ram_1_data), .str(register_14_q), .clk(CLK),
    .ld(register_13_q), .clr(R));  // open: sel
  Register #(.width(1)) register_18 (.D(register_13_q), .Q(register_18_q), .clk(CLK), .clr(R));  // open: en
  Register #(.width(32)) register_19 (.D(ram_1_data), .Q(register_19_q), .clk(CLK), .clr(R));  // open: en

  // Notes on the sheet:
  //   contents of rom_1 (hex, n*v repeats v):
  //   6a000000 4*0 61000000 4*0 62000000 4*0 6f000002 4*0 6b000000 4*0 6c000004 4*0 6d000008 4*0 50af02bc
  //   4*0 61000000 4*0 501f0294 4*0 62000000 4*0 63000000 4*0 29af0000 4*0 9910000 4*0 ed90000 4*0
  //   700e0000 4*0 502f0244 4*0 28af0000 4*0 8820000 4*0 eb80000 4*0 840e0000 4*0 272f0000 4*0 7710000 4*0
  //   ec70000 4*0 850e0000 4*0 26450000 4*0 3360000 4*0 32020001 4*0 40000140 4*0 ed90000 4*0 703e0000 4*0
  //   31010001 4*0 400000b4 4*0 3a0a0001 4*0 4000008c
  //   SHAMT
  //   REG_W
  //   REG_1
  //   REG_0
  //   DATA_W
  //   BANCO DE REGISTRADORES
  //   REG1_D
  //   REG0_D
  //   ULA
endmodule

module ULA (
  input  [31:0] DATA_0,
  input  [31:0] DATA_1,
  input  [3:0] ULA_OP,
  input  [4:0] shamt,
  output [31:0] ULA_OUT,
  output bge
);

  wire comparator_1_lt;
  wire [31:0] adder_1_out, multiplier_1_out, shifter_1_out, shifter_2_out, subtractor_1_out;

  Adder #(.width(32)) adder_1 (.a(DATA_0), .b(DATA_1), .out(adder_1_out));  // open: cin, cout
  Subtractor #(.width(32)) subtractor_1 (.a(DATA_1), .b(DATA_0), .out(subtractor_1_out));  // open: bin, bout
  Multiplier #(.width(32)) multiplier_1 (.a(DATA_1), .b(DATA_0), .out(multiplier_1_out));  // open: cin, cout
  Comparator #(.width(32), .mode("unsigned")) comparator_1 (
    .a(DATA_1), .b(DATA_0), .lt(comparator_1_lt));  // open: gt, eq
  Shifter #(.width(32)) shifter_1 (.in(DATA_0), .\dist (shamt), .out(shifter_1_out));
  Shifter #(.width(32), .shift("lr")) shifter_2 (.in(DATA_0), .\dist (shamt), .out(shifter_2_out));
  not not_1 (bge, comparator_1_lt);
  Multiplexer #(.select(4), .width(32)) multiplexer_1 (
    .in0(adder_1_out), .in1(subtractor_1_out), .in2(multiplier_1_out), .in3(adder_1_out),
    .in4(shifter_1_out), .in6(adder_1_out), .in8(shifter_2_out), .out(ULA_OUT), .sel(ULA_OP));  // open: in5, in7, in9, in10, in11, in12, in13, in14, in15, en
endmodule

module UC (
  input  E3,
  input  E2,
  input  E1,
  input  E0,
  output write_reg,
  output mux_ula,
  output branch,
  output jump,
  output mem_read,
  output mem_write,
  output [3:0] op_code
);

  wire and_1_out, and_2_out, and_3_out, not_1_out, not_2_out, not_3_out, not_4_out, not_5_out, not_6_out,
       not_7_out;

  not not_1 (not_1_out, E2);
  and and_1 (and_1_out, E1, not_2_out);
  not not_2 (not_2_out, E0);
  not not_3 (not_3_out, E2);
  and and_2 (and_2_out, not_3_out, E1, E0);
  and and_3 (and_3_out, E2, E1, not_4_out);
  not not_4 (not_4_out, E0);
  not not_5 (not_5_out, E1);
  and and_4 (branch, E2, not_5_out, E0);
  not not_6 (not_6_out, E1);
  and and_5 (jump, E2, not_6_out, not_7_out);
  not not_7 (not_7_out, E0);
  and and_6 (mem_write, E2, E1, E0);
  or or_1 (write_reg, not_1_out, and_1_out);
  or or_2 (mux_ula, and_2_out, and_3_out);

  assign mem_read = E3;
  assign op_code = {E3, E2, E1, E0};
endmodule

module UC_LITTLE (
  input  e3,
  input  e2,
  input  e1,
  input  e0,
  output j
);

  wire not_1_out, not_2_out, not_3_out;

  not not_1 (not_1_out, e3);
  not not_2 (not_2_out, e1);
  not not_3 (not_3_out, e0);
  and and_1 (j, not_1_out, e2, not_2_out, not_3_out);
endmodule
